// Logisim project ALU.circ as structural Verilog: 23 circuits, main circuit main
module main (
  input  [31:0] A,
  input  [31:0] B,
  input  [3:0] ALUSel,
  output OverFlow,
  output [31:0] Result,
  output Zero
);

  alu alu_1 (.in_1(A), .in_2(B), .out_5(Result), .in_3(ALUSel), .out_4(OverFlow), .out_6(Zero));
endmodule

module alu (
  input  [31:0] in_1,
  input  [31:0] in_2,
  input  [3:0] in_3,
  output out_4,
  output [31:0] out_5,
  output out_6
);

  wire l_32bitadder_baae1c1e_1_out_4, not_1_out, not_2_out, not_3_out, not_4_out, zerodetector_1_out_2;
  wire [0:0] lessthan_1_out_3;
  wire [31:0] l_32bitadder_baae1c1e_1_out_3, l_32bitand_e90cfa2b_1_out_3, l_32bitor_b958d8b4_1_out_3,
       l_32bitsubtractor_b0d52311_1_out_3, l_32bitxor_3ee865f2_1_out_3, lessthanunsigned_1_out_3,
       multiplier_1_out_3, multiplier_1_out_4, multiplierhigherunsigned_1_out_3, shiftleftlogical_1_out_3,
       shiftrightarith_1_out_3, shiftrightlogical_1_out_3;

  ShiftLeftLogical shiftleftlogical_1 (.in_1(in_1), .out_3(shiftleftlogical_1_out_3), .in_2(in_2[4:0]));
  ShiftRightLogical shiftrightlogical_1 (.in_1(in_1), .out_3(shiftrightlogical_1_out_3), .in_2(in_2[4:0]));
  ShiftRightArith shiftrightarith_1 (.in_1(in_1), .out_3(shiftrightarith_1_out_3), .in_2(in_2[4:0]));
  L_32bitAdder_baae1c1e l_32bitadder_baae1c1e_1 (
    .in_1(in_1), .in_2(in_2), .out_3(l_32bitadder_baae1c1e_1_out_3), .out_4(l_32bitadder_baae1c1e_1_out_4),
    .out_5(l_32bitadder_baae1c1e_1_out_4));
  not not_1 (not_1_out, in_3[3]);
  not not_2 (not_2_out, in_3[1]);
  not not_3 (not_3_out, in_3[2]);
  Multiplier multiplier_1 (.in_1(in_1), .in_2(in_2), .out_3(multiplier_1_out_3), .out_4(multiplier_1_out_4));
  MultiplierHigherUnsigned multiplierhigherunsigned_1 (
    .in_1(in_1), .in_2(in_2), .out_3(multiplierhigherunsigned_1_out_3));
  and and_1 (out_4, l_32bitadder_baae1c1e_1_out_4, not_4_out);
  not not_4 (not_4_out, in_3[0]);
  LessThanUnsigned lessthanunsigned_1 (.in_1(in_1), .in_2(in_2), .out_3(lessthanunsigned_1_out_3));
  LessThan lessthan_1 (.in_1(in_1), .in_2(in_2), .out_3(lessthan_1_out_3[0]));
  L_32bitXOR_3ee865f2 l_32bitxor_3ee865f2_1 (.in_2(in_1), .out_3(l_32bitxor_3ee865f2_1_out_3), .in_1(in_2));
  L_32bitOR_b958d8b4 l_32bitor_b958d8b4_1 (.in_2(in_1), .out_3(l_32bitor_b958d8b4_1_out_3), .in_1(in_2));
  L_32bitAND_e90cfa2b l_32bitand_e90cfa2b_1 (.in_2(in_1), .out_3(l_32bitand_e90cfa2b_1_out_3), .in_1(in_2));
  L_32bitSubtractor_b0d52311 l_32bitsubtractor_b0d52311_1 (
    .in_1(in_1), .out_3(l_32bitsubtractor_b0d52311_1_out_3), .in_2(in_2));
  MUX_16_1_32Bit_fa0b1cbf mux_16_1_32bit_fa0b1cbf_1 (
    .in_1(l_32bitadder_baae1c1e_1_out_3), .in_2(l_32bitsubtractor_b0d52311_1_out_3),
    .in_3(shiftleftlogical_1_out_3), .in_4(multiplier_1_out_4), .in_5({{31{1'b0}}, lessthan_1_out_3[0]}),
    .in_7(lessthanunsigned_1_out_3), .in_8(multiplierhigherunsigned_1_out_3),
    .in_9(l_32bitxor_3ee865f2_1_out_3), .in_10(multiplier_1_out_3), .in_11(shiftrightlogical_1_out_3),
    .in_12(shiftrightarith_1_out_3), .in_13(l_32bitor_b958d8b4_1_out_3), .in_15(l_32bitand_e90cfa2b_1_out_3),
    .in_16(in_2), .out_18(out_5), .in_17(in_3));  // open: in_6, in_14
  ZeroDetector zerodetector_1 (.in_1(out_5), .out_2(zerodetector_1_out_2));
  not not_5 (out_6, zerodetector_1_out_2);
endmodule

module L_32bitAdder_baae1c1e (
  input  [31:0] in_1,
  input  [31:0] in_2,
  output [31:0] out_3,
  output out_4,
  output out_5
);

  wire and_1_out, and_2_out, not_1_out, not_2_out, not_3_out;

  Adder #(.width(32)) adder_1 (.a(in_1), .b(in_2), .out(out_3), .cin(1'b0), .cout(out_4));
  not not_1 (not_1_out, in_1[31]);
  not not_2 (not_2_out, in_2[31]);
  not not_3 (not_3_out, out_3[31]);
  and and_1 (and_1_out, in_1[31], in_2[31], not_3_out);
  and and_2 (and_2_out, not_1_out, not_2_out, out_3[31]);
  or or_1 (out_5, and_1_out, and_2_out);
endmodule

module L_32bitSubtractor_b0d52311 (
  input  [31:0] in_1,
  input  [31:0] in_2,
  output [31:0] out_3
);

  Subtractor #(.width(32)) subtractor_1 (.a(in_1), .b(in_2), .out(out_3), .bin(1'b0));  // open: bout
endmodule

module L_8bitXOR_005ab9e0 (
  input  [7:0] in_1,
  input  [7:0] in_2,
  output [7:0] out_3
);

  xor xor_1 (out_3[7], in_1[7], in_2[7]);
  xor xor_2 (out_3[6], in_1[6], in_2[6]);
  xor xor_3 (out_3[5], in_1[5], in_2[5]);
  xor xor_4 (out_3[4], in_1[4], in_2[4]);
  xor xor_5 (out_3[3], in_1[3], in_2[3]);
  xor xor_6 (out_3[2], in_1[2], in_2[2]);
  xor xor_7 (out_3[1], in_1[1], in_2[1]);
  xor xor_8 (out_3[0], in_1[0], in_2[0]);
endmodule

module L_32bitXOR_3ee865f2 (
  input  [31:0] in_1,
  input  [31:0] in_2,
  output [31:0] out_3
);

  L_8bitXOR_005ab9e0 l_8bitxor_005ab9e0_1 (.in_1(in_2[31:24]), .in_2(in_1[31:24]), .out_3(out_3[31:24]));
  L_8bitXOR_005ab9e0 l_8bitxor_005ab9e0_2 (.in_1(in_2[23:16]), .in_2(in_1[23:16]), .out_3(out_3[23:16]));
  L_8bitXOR_005ab9e0 l_8bitxor_005ab9e0_3 (.in_1(in_2[15:8]), .in_2(in_1[15:8]), .out_3(out_3[15:8]));
  L_8bitXOR_005ab9e0 l_8bitxor_005ab9e0_4 (.in_1(in_2[7:0]), .in_2(in_1[7:0]), .out_3(out_3[7:0]));
endmodule

module L_8bitAND_9130299e (
  input  [7:0] in_1,
  input  [7:0] in_2,
  output [7:0] out_3
);

  and and_1 (out_3[7], in_1[7], in_2[7]);
  and and_2 (out_3[6], in_1[6], in_2[6]);
  and and_3 (out_3[5], in_1[5], in_2[5]);
  and and_4 (out_3[4], in_1[4], in_2[4]);
  and and_5 (out_3[3], in_1[3], in_2[3]);
  and and_6 (out_3[2], in_1[2], in_2[2]);
  and and_7 (out_3[1], in_1[1], in_2[1]);
  and and_8 (out_3[0], in_1[0], in_2[0]);
endmodule

module L_32bitAND_e90cfa2b (
  input  [31:0] in_1,
  input  [31:0] in_2,
  output [31:0] out_3
);

  L_8bitAND_9130299e l_8bitand_9130299e_1 (.in_1(in_2[31:24]), .in_2(in_1[31:24]), .out_3(out_3[31:24]));
  L_8bitAND_9130299e l_8bitand_9130299e_2 (.in_1(in_2[23:16]), .in_2(in_1[23:16]), .out_3(out_3[23:16]));
  L_8bitAND_9130299e l_8bitand_9130299e_3 (.in_1(in_2[15:8]), .in_2(in_1[15:8]), .out_3(out_3[15:8]));
  L_8bitAND_9130299e l_8bitand_9130299e_4 (.in_1(in_2[7:0]), .in_2(in_1[7:0]), .out_3(out_3[7:0]));
endmodule

module L_32bitOR_b958d8b4 (
  input  [31:0] in_1,
  input  [31:0] in_2,
  output [31:0] out_3
);

  L_8bitOR_35c60051 l_8bitor_35c60051_1 (.in_1(in_2[31:24]), .in_2(in_1[31:24]), .out_3(out_3[31:24]));
  L_8bitOR_35c60051 l_8bitor_35c60051_2 (.in_1(in_2[23:16]), .in_2(in_1[23:16]), .out_3(out_3[23:16]));
  L_8bitOR_35c60051 l_8bitor_35c60051_3 (.in_1(in_2[15:8]), .in_2(in_1[15:8]), .out_3(out_3[15:8]));
  L_8bitOR_35c60051 l_8bitor_35c60051_4 (.in_1(in_2[7:0]), .in_2(in_1[7:0]), .out_3(out_3[7:0]));
endmodule

module L_8bitOR_35c60051 (
  input  [7:0] in_1,
  input  [7:0] in_2,
  output [7:0] out_3
);

  or or_1 (out_3[7], in_1[7], in_2[7]);
  or or_2 (out_3[6], in_1[6], in_2[6]);
  or or_3 (out_3[5], in_1[5], in_2[5]);
  or or_4 (out_3[4], in_1[4], in_2[4]);
  or or_5 (out_3[3], in_1[3], in_2[3]);
  or or_6 (out_3[2], in_1[2], in_2[2]);
  or or_7 (out_3[1], in_1[1], in_2[1]);
  or or_8 (out_3[0], in_1[0], in_2[0]);
endmodule

module ShiftLeftLogical (
  input  [31:0] in_1,
  input  [4:0] in_2,
  output [31:0] out_3
);

  Shifter #(.width(32)) shifter_1 (.in(in_1), .\dist (in_2), .out(out_3));
endmodule

module ShiftRightLogical (
  input  [31:0] in_1,
  input  [4:0] in_2,
  output [31:0] out_3
);

  Shifter #(.width(32), .shift("lr")) shifter_1 (.in(in_1), .\dist (in_2), .out(out_3));
endmodule

module ShiftRightArith (
  input  [31:0] in_1,
  input  [4:0] in_2,
  output [31:0] out_3
);

  Shifter #(.width(32), .shift("ar")) shifter_1 (.in(in_1), .\dist (in_2), .out(out_3));
endmodule

module LessThan (
  input  [31:0] in_1,
  input  [31:0] in_2,
  output out_3
);

  wire and_1_out, comparator_1_eq, comparator_1_gt, comparator_1_lt;

  Comparator #(.width(32)) comparator_1 (
    .a(in_1), .b(in_2), .gt(comparator_1_gt), .eq(comparator_1_eq), .lt(comparator_1_lt));
  and and_1 (and_1_out, comparator_1_gt, comparator_1_eq);
  or or_1 (out_3, and_1_out, comparator_1_lt);
endmodule

module Multiplier (
  input  [31:0] in_1,
  input  [31:0] in_2,
  output [31:0] out_3,
  output [31:0] out_4
);

  Multiplier_part #(.width(32)) multiplier_1 (.a(in_1), .b(in_2), .out(out_3), .cin({32{1'b0}}), .cout(out_4));
endmodule

module MultiplierHigherUnsigned (
  input  [31:0] in_1,
  input  [31:0] in_2,
  output [31:0] out_3
);

  wire adder_1_cout, adder_4_cout, adder_5_cout, and_1_out, and_2_out;
  wire [31:0] adder_2_out, adder_3_out, adder_4_out, adder_5_out, adder_6_out, multiplier_1_cout,
       multiplier_1_out;

  Adder #(.width(1)) adder_1 (.a(in_1[0]), .b(in_2[0]), .cin(multiplier_1_out[31]), .cout(adder_1_cout));  // open: out
  Multiplier_part #(.width(32)) multiplier_1 (
    .a({1'b0, in_1[30:0]}), .b({1'b0, in_2[30:0]}), .out(multiplier_1_out), .cout(multiplier_1_cout));  // open: cin
  and and_1 (and_1_out, in_1[0], multiplier_1_out[31]);
  Adder #(.width(32)) adder_2 (
    .a(multiplier_1_cout), .b({2'b00, in_1[30:1]}), .out(adder_2_out), .cin(and_1_out));  // open: cout
  and and_2 (and_2_out, in_2[0], multiplier_1_out[31]);
  Adder #(.width(32)) adder_3 (
    .a(multiplier_1_cout), .b({2'b00, in_2[30:1]}), .out(adder_3_out), .cin(and_2_out));  // open: cout
  Adder #(.width(32)) adder_4 (
    .a(multiplier_1_cout), .b(32'h40000000), .out(adder_4_out), .cin(adder_1_cout), .cout(adder_4_cout));
  Adder #(.width(32)) adder_5 (
    .a({2'b00, in_1[30:1]}), .b({2'b00, in_2[30:1]}), .out(adder_5_out), .cin(adder_4_cout),
    .cout(adder_5_cout));
  MUX_4_1_32Bit_3fbd7dcb mux_4_1_32bit_3fbd7dcb_1 (
    .in_1(multiplier_1_cout), .in_2(adder_3_out), .in_3(adder_2_out), .in_4(adder_6_out), .out_6(out_3),
    .in_5({in_2[31], in_1[31]}));
  Adder #(.width(32)) adder_6 (.a(adder_5_out), .b(adder_4_out), .out(adder_6_out), .cin(adder_5_cout));  // open: cout
endmodule

module MUX_2_1_1Bit_7e204657 (
  input  A,
  input  B,
  input  A_sel,
  output out_4
);

  wire and_1_out, and_2_out;

  and and_1 (and_1_out, A, A_sel);
  and and_2 (and_2_out, ~A_sel, B);  // AND_Gate
  or or_1 (out_4, and_1_out, and_2_out);
endmodule

module MUX_2_1_32Bit_272e388b (
  input  [31:0] L_1_5c8fbffa,
  input  [31:0] L_0_c696acd8,
  input  in_3,
  output [31:0] out_4
);

  MUX_2_1_1Bit_7e204657 mux_2_1_1bit_7e204657_1 (
    .A(L_1_5c8fbffa[0]), .B(L_0_c696acd8[0]), .A_sel(in_3), .out_4(out_4[0]));
  MUX_2_1_1Bit_7e204657 mux_2_1_1bit_7e204657_2 (
    .A(L_1_5c8fbffa[1]), .B(L_0_c696acd8[1]), .A_sel(in_3), .out_4(out_4[1]));
  MUX_2_1_1Bit_7e204657 mux_2_1_1bit_7e204657_3 (
    .A(L_1_5c8fbffa[2]), .B(L_0_c696acd8[2]), .A_sel(in_3), .out_4(out_4[2]));
  MUX_2_1_1Bit_7e204657 mux_2_1_1bit_7e204657_4 (
    .A(L_1_5c8fbffa[3]), .B(L_0_c696acd8[3]), .A_sel(in_3), .out_4(out_4[3]));
  MUX_2_1_1Bit_7e204657 mux_2_1_1bit_7e204657_5 (
    .A(L_1_5c8fbffa[4]), .B(L_0_c696acd8[4]), .A_sel(in_3), .out_4(out_4[4]));
  MUX_2_1_1Bit_7e204657 mux_2_1_1bit_7e204657_6 (
    .A(L_1_5c8fbffa[5]), .B(L_0_c696acd8[5]), .A_sel(in_3), .out_4(out_4[5]));
  MUX_2_1_1Bit_7e204657 mux_2_1_1bit_7e204657_7 (
    .A(L_1_5c8fbffa[6]), .B(L_0_c696acd8[6]), .A_sel(in_3), .out_4(out_4[6]));
  MUX_2_1_1Bit_7e204657 mux_2_1_1bit_7e204657_8 (
    .A(L_1_5c8fbffa[7]), .B(L_0_c696acd8[7]), .A_sel(in_3), .out_4(out_4[7]));
  MUX_2_1_1Bit_7e204657 mux_2_1_1bit_7e204657_9 (
    .A(L_1_5c8fbffa[8]), .B(L_0_c696acd8[8]), .A_sel(in_3), .out_4(out_4[8]));
  MUX_2_1_1Bit_7e204657 mux_2_1_1bit_7e204657_10 (
    .A(L_1_5c8fbffa[9]), .B(L_0_c696acd8[9]), .A_sel(in_3), .out_4(out_4[9]));
  MUX_2_1_1Bit_7e204657 mux_2_1_1bit_7e204657_11 (
    .A(L_1_5c8fbffa[10]), .B(L_0_c696acd8[10]), .A_sel(in_3), .out_4(out_4[10]));
  MUX_2_1_1Bit_7e204657 mux_2_1_1bit_7e204657_12 (
    .A(L_1_5c8fbffa[11]), .B(L_0_c696acd8[11]), .A_sel(in_3), .out_4(out_4[11]));
  MUX_2_1_1Bit_7e204657 mux_2_1_1bit_7e204657_13 (
    .A(L_1_5c8fbffa[12]), .B(L_0_c696acd8[12]), .A_sel(in_3), .out_4(out_4[12]));
  MUX_2_1_1Bit_7e204657 mux_2_1_1bit_7e204657_14 (
    .A(L_1_5c8fbffa[13]), .B(L_0_c696acd8[13]), .A_sel(in_3), .out_4(out_4[13]));
  MUX_2_1_1Bit_7e204657 mux_2_1_1bit_7e204657_15 (
    .A(L_1_5c8fbffa[14]), .B(L_0_c696acd8[14]), .A_sel(in_3), .out_4(out_4[14]));
  MUX_2_1_1Bit_7e204657 mux_2_1_1bit_7e204657_16 (
    .A(L_1_5c8fbffa[15]), .B(L_0_c696acd8[15]), .A_sel(in_3), .out_4(out_4[15]));
  MUX_2_1_1Bit_7e204657 mux_2_1_1bit_7e204657_17 (
    .A(L_1_5c8fbffa[16]), .B(L_0_c696acd8[16]), .A_sel(in_3), .out_4(out_4[16]));
  MUX_2_1_1Bit_7e204657 mux_2_1_1bit_7e204657_18 (
    .A(L_1_5c8fbffa[17]), .B(L_0_c696acd8[17]), .A_sel(in_3), .out_4(out_4[17]));
  MUX_2_1_1Bit_7e204657 mux_2_1_1bit_7e204657_19 (
    .A(L_1_5c8fbffa[18]), .B(L_0_c696acd8[18]), .A_sel(in_3), .out_4(out_4[18]));
  MUX_2_1_1Bit_7e204657 mux_2_1_1bit_7e204657_20 (
    .A(L_1_5c8fbffa[19]), .B(L_0_c696acd8[19]), .A_sel(in_3), .out_4(out_4[19]));
  MUX_2_1_1Bit_7e204657 mux_2_1_1bit_7e204657_21 (
    .A(L_1_5c8fbffa[20]), .B(L_0_c696acd8[20]), .A_sel(in_3), .out_4(out_4[20]));
  MUX_2_1_1Bit_7e204657 mux_2_1_1bit_7e204657_22 (
    .A(L_1_5c8fbffa[21]), .B(L_0_c696acd8[21]), .A_sel(in_3), .out_4(out_4[21]));
  MUX_2_1_1Bit_7e204657 mux_2_1_1bit_7e204657_23 (
    .A(L_1_5c8fbffa[22]), .B(L_0_c696acd8[22]), .A_sel(in_3), .out_4(out_4[22]));
  MUX_2_1_1Bit_7e204657 mux_2_1_1bit_7e204657_24 (
    .A(L_1_5c8fbffa[23]), .B(L_0_c696acd8[23]), .A_sel(in_3), .out_4(out_4[23]));
  MUX_2_1_1Bit_7e204657 mux_2_1_1bit_7e204657_25 (
    .A(L_1_5c8fbffa[24]), .B(L_0_c696acd8[24]), .A_sel(in_3), .out_4(out_4[24]));
  MUX_2_1_1Bit_7e204657 mux_2_1_1bit_7e204657_26 (
    .A(L_1_5c8fbffa[25]), .B(L_0_c696acd8[25]), .A_sel(in_3), .out_4(out_4[25]));
  MUX_2_1_1Bit_7e204657 mux_2_1_1bit_7e204657_27 (
    .A(L_1_5c8fbffa[26]), .B(L_0_c696acd8[26]), .A_sel(in_3), .out_4(out_4[26]));
  MUX_2_1_1Bit_7e204657 mux_2_1_1bit_7e204657_28 (
    .A(L_1_5c8fbffa[27]), .B(L_0_c696acd8[27]), .A_sel(in_3), .out_4(out_4[27]));
  MUX_2_1_1Bit_7e204657 mux_2_1_1bit_7e204657_29 (
    .A(L_1_5c8fbffa[28]), .B(L_0_c696acd8[28]), .A_sel(in_3), .out_4(out_4[28]));
  MUX_2_1_1Bit_7e204657 mux_2_1_1bit_7e204657_30 (
    .A(L_1_5c8fbffa[29]), .B(L_0_c696acd8[29]), .A_sel(in_3), .out_4(out_4[29]));
  MUX_2_1_1Bit_7e204657 mux_2_1_1bit_7e204657_31 (
    .A(L_1_5c8fbffa[30]), .B(L_0_c696acd8[30]), .A_sel(in_3), .out_4(out_4[30]));
  MUX_2_1_1Bit_7e204657 mux_2_1_1bit_7e204657_32 (
    .A(L_1_5c8fbffa[31]), .B(L_0_c696acd8[31]), .A_sel(in_3), .out_4(out_4[31]));
endmodule

module MUX_8_1_32Bit_6d3ee3a9 (
  input  [31:0] L_7_44684acf,
  input  [31:0] in_2,
  input  [31:0] in_3,
  input  [31:0] in_4,
  input  [31:0] in_5,
  input  [31:0] in_6,
  input  [31:0] in_7,
  input  [31:0] L_0_c696acd8,
  input  [2:0] in_9,
  output [31:0] out_10
);

  wire [31:0] mux_2_1_32bit_272e388b_1_out_4, mux_2_1_32bit_272e388b_2_out_4, mux_2_1_32bit_272e388b_3_out_4,
       mux_2_1_32bit_272e388b_4_out_4, mux_2_1_32bit_272e388b_5_out_4, mux_2_1_32bit_272e388b_6_out_4;

  MUX_2_1_32Bit_272e388b mux_2_1_32bit_272e388b_1 (
    .L_1_5c8fbffa(L_7_44684acf), .L_0_c696acd8(in_2), .in_3(in_9[0]), .out_4(mux_2_1_32bit_272e388b_1_out_4));
  MUX_2_1_32Bit_272e388b mux_2_1_32bit_272e388b_2 (
    .L_1_5c8fbffa(in_3), .L_0_c696acd8(in_4), .in_3(in_9[0]), .out_4(mux_2_1_32bit_272e388b_2_out_4));
  MUX_2_1_32Bit_272e388b mux_2_1_32bit_272e388b_3 (
    .L_1_5c8fbffa(in_5), .L_0_c696acd8(in_6), .in_3(in_9[0]), .out_4(mux_2_1_32bit_272e388b_3_out_4));
  MUX_2_1_32Bit_272e388b mux_2_1_32bit_272e388b_4 (
    .L_1_5c8fbffa(in_7), .L_0_c696acd8(L_0_c696acd8), .in_3(in_9[0]), .out_4(mux_2_1_32bit_272e388b_4_out_4));
  MUX_2_1_32Bit_272e388b mux_2_1_32bit_272e388b_5 (
    .L_1_5c8fbffa(mux_2_1_32bit_272e388b_1_out_4), .L_0_c696acd8(mux_2_1_32bit_272e388b_2_out_4),
    .in_3(in_9[1]), .out_4(mux_2_1_32bit_272e388b_5_out_4));
  MUX_2_1_32Bit_272e388b mux_2_1_32bit_272e388b_6 (
    .L_1_5c8fbffa(mux_2_1_32bit_272e388b_3_out_4), .L_0_c696acd8(mux_2_1_32bit_272e388b_4_out_4),
    .in_3(in_9[1]), .out_4(mux_2_1_32bit_272e388b_6_out_4));
  MUX_2_1_32Bit_272e388b mux_2_1_32bit_272e388b_7 (
    .L_1_5c8fbffa(mux_2_1_32bit_272e388b_5_out_4), .L_0_c696acd8(mux_2_1_32bit_272e388b_6_out_4),
    .in_3(in_9[2]), .out_4(out_10));
endmodule

module MUX_16_1_32Bit_fa0b1cbf (
  input  [31:0] in_1,
  input  [31:0] in_2,
  input  [31:0] in_3,
  input  [31:0] in_4,
  input  [31:0] in_5,
  input  [31:0] in_6,
  input  [31:0] in_7,
  input  [31:0] in_8,
  input  [31:0] in_9,
  input  [31:0] in_10,
  input  [31:0] in_11,
  input  [31:0] in_12,
  input  [31:0] in_13,
  input  [31:0] in_14,
  input  [31:0] in_15,
  input  [31:0] in_16,
  input  [3:0] in_17,
  output [31:0] out_18
);

  wire [31:0] mux_8_1_32bit_6d3ee3a9_1_out_10, mux_8_1_32bit_6d3ee3a9_2_out_10;

  MUX_8_1_32Bit_6d3ee3a9 mux_8_1_32bit_6d3ee3a9_1 (
    .L_7_44684acf(in_15), .in_2(in_13), .in_3(in_11), .in_4(in_9), .in_5(in_7), .in_6(in_5), .in_7(in_3),
    .L_0_c696acd8(in_1), .in_9(in_17[2:0]), .out_10(mux_8_1_32bit_6d3ee3a9_1_out_10));
  MUX_8_1_32Bit_6d3ee3a9 mux_8_1_32bit_6d3ee3a9_2 (
    .L_7_44684acf(in_16), .in_2(in_14), .in_3(in_12), .in_4(in_10), .in_5(in_8), .in_6(in_6), .in_7(in_4),
    .L_0_c696acd8(in_2), .in_9(in_17[2:0]), .out_10(mux_8_1_32bit_6d3ee3a9_2_out_10));
  MUX_2_1_32Bit_272e388b mux_2_1_32bit_272e388b_1 (
    .L_1_5c8fbffa(mux_8_1_32bit_6d3ee3a9_2_out_10), .L_0_c696acd8(mux_8_1_32bit_6d3ee3a9_1_out_10),
    .in_3(in_17[3]), .out_4(out_18));
endmodule

module MUX_4_1_32Bit_3fbd7dcb (
  input  [31:0] in_1,
  input  [31:0] in_2,
  input  [31:0] in_3,
  input  [31:0] in_4,
  input  [1:0] in_5,
  output [31:0] out_6
);

  wire [31:0] mux_2_1_32bit_272e388b_1_out_4, mux_2_1_32bit_272e388b_2_out_4;

  MUX_2_1_32Bit_272e388b mux_2_1_32bit_272e388b_1 (
    .L_1_5c8fbffa(in_2), .L_0_c696acd8(in_1), .in_3(in_5[0]), .out_4(mux_2_1_32bit_272e388b_1_out_4));
  MUX_2_1_32Bit_272e388b mux_2_1_32bit_272e388b_2 (
    .L_1_5c8fbffa(in_4), .L_0_c696acd8(in_3), .in_3(in_5[0]), .out_4(mux_2_1_32bit_272e388b_2_out_4));
  MUX_2_1_32Bit_272e388b mux_2_1_32bit_272e388b_3 (
    .L_1_5c8fbffa(mux_2_1_32bit_272e388b_2_out_4), .L_0_c696acd8(mux_2_1_32bit_272e388b_1_out_4),
    .in_3(in_5[1]), .out_4(out_6));
endmodule

module ZeroDetector (
  input  [31:0] in_1,
  output out_2
);

  wire not_1_out, not_2_out, not_3_out, not_4_out, not_5_out, not_6_out, not_7_out, not_8_out, not_9_out,
       not_10_out, not_11_out, not_12_out, not_13_out, not_14_out, not_15_out, not_16_out, not_17_out,
       not_18_out, not_19_out, not_20_out, not_21_out, not_22_out, not_23_out, not_24_out, not_25_out,
       not_26_out, not_27_out, not_28_out, not_29_out, not_30_out, not_31_out, not_32_out;

  not not_1 (not_1_out, in_1[0]);
  not not_2 (not_2_out, in_1[1]);
  not not_3 (not_3_out, in_1[2]);
  not not_4 (not_4_out, in_1[3]);
  not not_5 (not_5_out, in_1[4]);
  not not_6 (not_6_out, in_1[5]);
  not not_7 (not_7_out, in_1[6]);
  not not_8 (not_8_out, in_1[7]);
  not not_9 (not_9_out, in_1[8]);
  not not_10 (not_10_out, in_1[9]);
  not not_11 (not_11_out, in_1[10]);
  not not_12 (not_12_out, in_1[11]);
  not not_13 (not_13_out, in_1[12]);
  not not_14 (not_14_out, in_1[13]);
  not not_15 (not_15_out, in_1[14]);
  not not_16 (not_16_out, in_1[15]);
  not not_17 (not_17_out, in_1[16]);
  not not_18 (not_18_out, in_1[17]);
  not not_19 (not_19_out, in_1[18]);
  not not_20 (not_20_out, in_1[19]);
  not not_21 (not_21_out, in_1[20]);
  not not_22 (not_22_out, in_1[21]);
  not not_23 (not_23_out, in_1[22]);
  not not_24 (not_24_out, in_1[23]);
  not not_25 (not_25_out, in_1[24]);
  not not_26 (not_26_out, in_1[25]);
  not not_27 (not_27_out, in_1[26]);
  not not_28 (not_28_out, in_1[27]);
  not not_29 (not_29_out, in_1[28]);
  not not_30 (not_30_out, in_1[29]);
  not not_31 (not_31_out, in_1[30]);
  not not_32 (not_32_out, in_1[31]);
  and and_1 (out_2, not_1_out, not_2_out, not_3_out, not_4_out, not_5_out, not_6_out, not_7_out, not_8_out, not_9_out, not_10_out, not_11_out, not_12_out, not_13_out, not_14_out, not_15_out, not_16_out, not_18_out, not_19_out, not_20_out, not_21_out, not_22_out, not_23_out, not_24_out, not_25_out, not_26_out, not_27_out, not_28_out, not_29_out, not_30_out, not_31_out, not_32_out, not_17_out);
endmodule

module LessThanUnsigned (
  input  [31:0] in_1,
  input  [31:0] in_2,
  output [31:0] out_3
);

  wire lessthan_1_out_3;

  LessThan lessthan_1 (.in_1({1'b0, in_1[30:0]}), .in_2({1'b0, in_2[30:0]}), .out_3(lessthan_1_out_3));
  Multiplexer #(.select(2), .enable("false")) multiplexer_1 (
    .in0(lessthan_1_out_3), .in1(1'b0), .in2(1'b1), .in3(lessthan_1_out_3), .out(out_3[0]),
    .sel({in_2[31], in_1[31]}));

  assign out_3[31:1] = {31{1'b0}};
endmodule
