// Logisim project processor.circ as structural Verilog: 2 circuits, main circuit main
module main (
  input  in_1
);

  wire alu_1_out_6, and_1_out, clock_1_out, control_1_alusrc, control_1_load, control_1_pcsrc,
       control_1_store, control_1_write;
  wire [3:0] control_1_aluop;
  wire [4:0] control_1_rd, control_1_rs1, control_1_rs2;
  wire [23:0] adder_1_out, bit_extender_1_out, bit_extender_2_out, multiplexer_3_out, PC_q;
  wire [31:0] alu_1_out_5, control_1_imm, IMem_data, Memory_dout, multiplexer_2_out, registerfile_1_p4,
       registerfile_1_p7, registerfile_1_p8;

  Clock clock_1 (.out(clock_1_out));
  Register #(.width(24)) PC (.D(adder_1_out), .en(1'b1), .clk(clock_1_out), .Q(PC_q), .clr(in_1));
  ROM #(.addrWidth(24), .dataWidth(32)) IMem (.addr(PC_q), .data(IMem_data));
  Control control_1 (
    .ALUSrc(control_1_alusrc), .Write(control_1_write), .Store(control_1_store), .Load(control_1_load),
    .PCSrc(control_1_pcsrc), .ALUOp(control_1_aluop), .rd(control_1_rd), .Imm(control_1_imm),
    .rs1(control_1_rs1), .rs2(control_1_rs2), .in_1(IMem_data));
  Bit_Extender #(.in_width(32), .out_width(24), .\type ("input")) bit_extender_1 (
    .in(control_1_imm), .out(bit_extender_1_out));  // open: extend
  // registerfile registerfile_1: pin names not known; wires that end beside it: control_1_rs1, control_1_rs2, control_1_rd, registerfile_1_p4, clock_1_out, control_1_write, registerfile_1_p7, registerfile_1_p8
  Multiplexer #(.width(32)) multiplexer_1 (
    .in0(alu_1_out_5), .in1(Memory_dout), .out(registerfile_1_p4), .sel(control_1_load), .en(1'b1));
  Multiplexer #(.width(32)) multiplexer_2 (
    .in0(registerfile_1_p8), .in1(control_1_imm), .out(multiplexer_2_out), .sel(control_1_alusrc), .en(1'b1));
  Multiplexer #(.width(24)) multiplexer_3 (
    .in0(24'h1), .in1(bit_extender_1_out), .out(multiplexer_3_out), .sel(and_1_out), .en(1'b1));
  and and_1 (and_1_out, control_1_pcsrc, ~alu_1_out_6);  // AND_Gate
  alu alu_1 (
    .in_1(registerfile_1_p7), .in_2(multiplexer_2_out), .out_5(alu_1_out_5), .in_3(control_1_aluop),
    .out_6(alu_1_out_6));  // open: out_4
  Adder #(.width(24)) adder_1 (.a(multiplexer_3_out), .b(PC_q), .out(adder_1_out));  // open: cin, cout
  RAM #(.addrWidth(24), .dataWidth(32), .databus("bibus")) Memory (
    .addr(bit_extender_2_out), .we(control_1_store), .oe(control_1_load), .clk(clock_1_out),
    .din(registerfile_1_p8), .dout(Memory_dout));
  Bit_Extender #(.in_width(32), .out_width(24), .\type ("input")) bit_extender_2 (
    .in(alu_1_out_5), .out(bit_extender_2_out));  // open: extend

  // Notes on the sheet:
  //   contents of IMem (hex, n*v repeats v):
  //   1400293 200413 100393 100513 828c63 a38333 407303b3 600533 fff28293 fe0006e3 602123
endmodule

module Control (
  input  [31:0] in_1,
  output ALUSrc,
  output Write,
  output Store,
  output Load,
  output PCSrc,
  output [3:0] ALUOp,
  output [4:0] rd,
  output [31:0] Imm,
  output [4:0] rs1,
  output [4:0] rs2
);

  wire and_1_out, and_2_out, and_3_out;
  wire [3:3] or_1_out;
  wire [11:0] multiplexer_1_out, shifter_1_out;

  and and_1 (and_1_out, in_1[30], in_1[4], in_1[5], ~in_1[6]);  // AND_Gate
  and and_2 (and_2_out, ~in_1[4], in_1[5], in_1[6]);  // AND_Gate
  or or_1 (or_1_out[3], and_1_out, and_2_out);
  Shifter #(.width(12), .shift("ar")) shifter_1 (
    .in({in_1[31], in_1[7], in_1[30:25], in_1[11:8]}), .\dist (4'b0001), .out(shifter_1_out));
  and and_3 (and_3_out, ~in_1[4], ~in_1[6]);  // AND_Gate
  Multiplexer #(.select(3), .width(12), .enable("false")) multiplexer_1 (
    .in0(in_1[31:20]), .in1(in_1[31:20]), .in2({in_1[31:25], in_1[11:7]}), .in3({12{1'b0}}),
    .in4({12{1'b0}}), .in5({12{1'b0}}), .in6(shifter_1_out), .in7({12{1'b0}}), .out(multiplexer_1_out),
    .sel(in_1[6:4]));
  Multiplexer #(.width(4), .enable("false")) multiplexer_2 (
    .in0({or_1_out[3], in_1[14:12]}), .in1(4'b0000), .out(ALUOp), .sel(and_3_out));
  assign Imm = {{20{multiplexer_1_out[11]}}, multiplexer_1_out};  // Bit_Extender bit_extender_1
  or or_2 (ALUSrc, and_3_out, ~in_1[5]);  // OR_Gate
  or or_3 (Write, in_1[4], ~in_1[5]);  // OR_Gate
  and and_4 (Store, ~in_1[4], in_1[5], ~in_1[6]);  // AND_Gate
  and and_5 (Load, ~in_1[4], ~in_1[5]);  // AND_Gate

  assign PCSrc = in_1[6];
  assign rd = in_1[11:7];
  assign rs1 = in_1[19:15];
  assign rs2 = in_1[24:20];

  // Notes on the sheet:
  //   S type imm
  //   B type imm
  //   I type imm
endmodule
