// Logisim project register.circ as structural Verilog: 3 circuits, main circuit main
module main (
  input  RegWEn,
  input  [4:0] rs1,
  input  [4:0] rs2,
  input  [4:0] rd,
  input  [31:0] Write_Data,
  output [31:0] Read_Data_1,
  output [31:0] Read_Data_2
);

  wire Clock_out;

  Clock Clock (.out(Clock_out));
  registerfile registerfile_1 (
    .RegWEn(RegWEn), .Write_Data(Write_Data), .rd(rd), .Read_Data_1(Read_Data_1), .Read_Data_2(Read_Data_2),
    .rs2(rs2), .rs1(rs1));
endmodule

module registerfile (
  input  RegWEn,
  input  [31:0] Write_Data,
  input  [4:0] rs1,
  input  [4:0] rd,
  input  [4:0] rs2,
  output [31:0] Read_Data_1,
  output [31:0] Read_Data_2
);

  wire clock_1_out, demultiplexer_1_out0, demultiplexer_1_out1, demultiplexer_1_out2, demultiplexer_1_out5,
       demultiplexer_1_out6, demultiplexer_1_out7, demultiplexer_1_out8, demultiplexer_1_out9,
       demultiplexer_1_out10;
  wire [31:0] register_1_out_5, register_2_out_5, register_3_out_5, register_4_out_5, register_5_out_5,
       register_6_out_5, register_7_out_5, register_8_out_5, register_9_out_5;

  Clock clock_1 (.out(clock_1_out));
  Demultiplexer #(.select(4), .enable("false")) demultiplexer_1 (
    .out0(demultiplexer_1_out0), .out1(demultiplexer_1_out1), .out2(demultiplexer_1_out2),
    .out5(demultiplexer_1_out5), .out6(demultiplexer_1_out6), .out7(demultiplexer_1_out7),
    .out8(demultiplexer_1_out8), .out9(demultiplexer_1_out9), .out10(demultiplexer_1_out10), .in(RegWEn),
    .sel(rd[3:0]));  // open: out3, out4, out11, out12, out13, out14, out15
  register register_1 (
    .in_1({32{1'b0}}), .out_5(register_1_out_5), .in_2(demultiplexer_1_out0), .in_3(clock_1_out), .in_4(1'b0));
  register register_2 (
    .in_1(Write_Data), .out_5(register_2_out_5), .in_2(demultiplexer_1_out1), .in_3(clock_1_out), .in_4(1'b0));
  register register_3 (
    .in_1(Write_Data), .out_5(register_3_out_5), .in_2(demultiplexer_1_out2), .in_3(clock_1_out), .in_4(1'b0));
  register register_4 (
    .in_1(Write_Data), .out_5(register_4_out_5), .in_2(demultiplexer_1_out5), .in_3(clock_1_out), .in_4(1'b0));
  register register_5 (
    .in_1(Write_Data), .out_5(register_5_out_5), .in_2(demultiplexer_1_out6), .in_3(clock_1_out), .in_4(1'b0));
  register register_6 (
    .in_1(Write_Data), .out_5(register_6_out_5), .in_2(demultiplexer_1_out7), .in_3(clock_1_out), .in_4(1'b0));
  register register_7 (
    .in_1(Write_Data), .out_5(register_7_out_5), .in_2(demultiplexer_1_out8), .in_3(clock_1_out), .in_4(1'b0));
  register register_8 (
    .in_1(Write_Data), .out_5(register_8_out_5), .in_2(demultiplexer_1_out9), .in_3(clock_1_out), .in_4(1'b0));
  register register_9 (
    .in_1(Write_Data), .out_5(register_9_out_5), .in_2(demultiplexer_1_out10), .in_3(clock_1_out), .in_4(1'b0));
  Multiplexer #(.select(4), .width(32)) multiplexer_1 (
    .in0(register_1_out_5), .in1(register_2_out_5), .in2(register_3_out_5), .in3({32{1'b0}}),
    .in4({32{1'b0}}), .in5(register_4_out_5), .in6(register_5_out_5), .in7(register_6_out_5),
    .in8(register_7_out_5), .in9(register_8_out_5), .in10(register_9_out_5), .in11({32{1'b0}}),
    .in12({32{1'b0}}), .in13({32{1'b0}}), .in14({32{1'b0}}), .in15({32{1'b0}}), .out(Read_Data_1),
    .sel(rs1[3:0]), .en(1'b1));
  Multiplexer #(.select(4), .width(32)) multiplexer_2 (
    .in0(register_1_out_5), .in1(register_2_out_5), .in2(register_3_out_5), .in3({32{1'b0}}),
    .in4({32{1'b0}}), .in5(register_4_out_5), .in6(register_5_out_5), .in7(register_6_out_5),
    .in8(register_7_out_5), .in9(register_8_out_5), .in10(register_9_out_5), .in11({32{1'b0}}),
    .in12({32{1'b0}}), .in13({32{1'b0}}), .in14({32{1'b0}}), .in15({32{1'b0}}), .out(Read_Data_2),
    .sel(rs2[3:0]), .en(1'b1));
endmodule

module register (
  input  [31:0] in_1,
  input  in_2,
  input  in_3,
  input  in_4,
  output [31:0] out_5
);

  Register #(.width(32)) register_1 (.D(in_1), .en(in_2), .clk(in_3), .Q(out_5), .clr(in_4));
endmodule
